# Fritzing sketch BCMS (saved by Fritzing 0.9.3b)
circuit board: 8.46667cm x 5.64444cm
breadboards: 1

parts:
  ESP8266_NODEMCU = ESP8266 NodeMCU LoLin module
  6V_solar_cell = SOLAR-IXYS [package=solarbit-12x1]
  TP4650 = TP4056 [chip_label=TP4056 package="DIP (Dual Inline) [THT]"]
  Current_Sensor = Current Sensor 5A
  DHT11 = DHT11 Humitidy and Temperature Sensor (3 pins)
  U2 = LIPO-110mAh [package=lipo-110]
  Current_Sensor1 = Current Sensor 5A
  MUX1 = 74HC4051 [package="DIP (Dual Inline) [THT]"]

nets:
  N1: ESP8266_NODEMCU.D0, DHT11.Signal
  N2: ESP8266_NODEMCU.D2, MUX1.A
  N3: ESP8266_NODEMCU.D3, MUX1.B
  N4: ESP8266_NODEMCU.D4, MUX1.C
  VCC: ESP8266_NODEMCU.Vin, TP4650.pin3, Current_Sensor.VCC, DHT11.Plus, Current_Sensor1.VCC, MUX1.VDD
  GND: ESP8266_NODEMCU.GND, 6V_solar_cell.A, TP4650.pin2, TP4650.pin6, Current_Sensor.GND, DHT11.Gnd, Current_Sensor1.GND, MUX1.VSS
  N5: ESP8266_NODEMCU.A0, MUX1.IO
  N6: 6V_solar_cell.C, Current_Sensor.2, Current_Sensor.OUT, MUX1.IO2
  N7: TP4650.pin1, Current_Sensor.1
  N8: TP4650.pin4, Current_Sensor1.1
  N9: TP4650.pin5, U2.-
  N10: U2.+, Current_Sensor1.2, Current_Sensor1.OUT, MUX1.IO1

custom parts:
  ESP8266 NodeMCU LoLin module: ESP8266 based NodeMCU
  TP4056: A DIP stand-in part for whatever IC you want. With 6 pins on a 300mil dual inline package (DIP) footprint.
  DHT11 Humitidy and Temperature Sensor (3 pins): DHT11 Humidity and Temperature Sensor (3 pins).
  74HC4051: 8 channel analog multiplexer/demultiplexer
